# Fritzing sketch iTilt (saved by Fritzing 0.9.4)
breadboards: 1

parts:
  GY1 = MPU-6050 Board GY-521 [form="♀ (female)" package=THT]
  BAT1 = 18650 battery holder [package=battery-18650-kit]
  DS1 = DS18B20 1-Wire Temperature Sensor [part_number=DS18B20]
  R1 = Resistor [tolerance=±5% resistance=4.7k package="2010 [SMD]"]
  S1 = SPST Switch [package=switch-spdt_lock.007s]
  R2 = Resistor [package="2010 [SMD]"]
  R3 = Resistor [tolerance=±5% resistance=220 package="2010 [SMD]"]
  U1 = lolin

nets:
  N1: GY1.pin1, DS1.VDD, R1.Pin_1, U1.connector4
  N2: GY1.pin2, DS1.GND, R3.Pin_1, U1.connector37
  N3: GY1.pin3, U1.connector33
  N4: GY1.pin4, U1.connector32
  N5: BAT1.+, R2.Pin_0, U1.connector16
  N6: BAT1.-, S1.P
  N7: DS1.DQ, U1.connector5
  N8: S1.O, U1.connector17
  N9: R2.Pin_1, R3.Pin_0, U1.connector2

notes:
  DS18B20
  MPU6050
  4.7 K OHMS
  Togle Switch
  4.7KOHMS
  10 KOHMS
  ESP32 TTG Koala

custom parts:
  MPU-6050 Board GY-521: Acelerometro y Giroscopio MPU-6050 Board GY-521
  18650 battery holder: 18650 Battery Holder
  Resistor: Resistor Basic schematic elements and footprints for 0603, 1206, and PTH resistors.
